// Logisim project 8bit_computer.circ as structural Verilog: 1 circuit, main circuit main
module main (
);

  wire and_1_out, and_2_out, and_3_out, and_4_out, and_5_out, and_6_out, and_7_out, and_8_out, and_9_out,
       and_10_out, and_11_out, and_12_out, and_13_out, and_14_out, and_15_out, and_16_out, and_17_out,
       and_18_out, and_19_out, and_20_out, and_21_out, and_22_out, and_23_out, and_24_out, and_25_out,
       and_26_out, and_27_out, and_28_out, and_29_out, and_30_out, and_31_out, and_32_out, and_33_out,
       and_34_out, and_35_out, and_36_out, and_37_out, and_38_out, and_39_out, and_40_out, and_41_out,
       and_42_out, and_43_out, and_44_out, and_45_out, and_46_out, and_47_out, and_48_out, and_49_out,
       and_50_out, and_51_out, and_52_out, and_53_out, and_54_out, and_55_out, and_56_out, and_57_out,
       and_58_out, and_59_out, and_60_out, and_61_out, and_62_out, and_63_out, and_64_out, and_65_out,
       and_66_out, and_67_out, and_68_out, and_69_out, and_70_out, and_71_out, and_72_out, and_73_out,
       and_74_out, and_75_out, and_76_out, and_77_out, and_78_out, and_79_out, and_80_out, and_81_out,
       and_82_out, and_83_out, and_84_out, and_85_out, and_86_out, and_87_out, and_88_out, and_89_out,
       and_90_out, and_91_out, and_92_out, and_93_out, and_94_out, and_95_out, and_96_out, and_97_out,
       and_98_out, and_99_out, and_100_out, and_101_out, and_102_out, and_103_out, and_104_out, and_105_out,
       and_106_out, and_107_out, and_108_out, and_109_out, and_110_out, and_111_out, and_112_out,
       and_113_out, and_114_out, and_115_out, and_116_out, and_117_out, and_118_out, and_119_out,
       and_120_out, and_121_out, and_122_out, and_123_out, and_124_out, and_125_out, and_126_out,
       and_127_out, and_128_out, and_129_out, and_130_out, and_131_out, and_132_out, and_133_out,
       and_134_out, and_135_out, and_136_out, and_137_out, and_138_out, and_139_out, and_140_out,
       and_141_out, and_142_out, and_143_out, and_144_out, and_145_out, and_146_out, and_147_out,
       and_148_out, and_149_out, and_150_out, and_151_out, and_152_out, and_153_out, and_154_out,
       and_155_out, and_156_out, and_157_out, and_158_out, and_159_out, and_160_out, and_161_out,
       and_162_out, and_163_out, and_164_out, and_165_out, and_166_out, and_167_out, and_168_out,
       and_169_out, and_170_out, and_171_out, and_172_out, and_173_out, and_174_out, and_175_out,
       and_176_out, and_177_out, and_178_out, and_179_out, and_180_out, and_181_out, and_182_out,
       and_183_out, and_184_out, and_185_out, and_186_out, and_187_out, and_188_out, and_189_out,
       and_190_out, and_191_out, and_192_out, and_193_out, and_194_out, and_195_out, and_196_out,
       and_197_out, and_198_out, and_199_out, and_200_out, and_201_out, and_202_out, and_203_out,
       and_204_out, and_205_out, and_206_out, and_207_out, and_208_out, and_209_out, and_210_out,
       and_211_out, and_212_out, and_213_out, and_214_out, and_215_out, and_216_out, and_217_out,
       and_218_out, and_219_out, and_220_out, and_221_out, and_222_out, and_223_out, and_224_out,
       and_225_out, and_226_out, and_227_out, and_228_out, and_229_out, and_230_out, and_231_out,
       and_232_out, and_233_out, and_234_out, and_235_out, and_236_out, and_237_out, and_238_out,
       and_239_out, and_240_out, and_241_out, and_242_out, and_243_out, and_244_out, and_245_out,
       and_246_out, and_247_out, and_248_out, and_249_out, and_250_out, and_251_out, and_252_out,
       and_253_out, and_254_out, and_255_out, and_256_out, and_257_out, and_258_out, and_259_out,
       and_260_out, and_261_out, and_262_out, and_263_out, and_264_out, and_265_out, and_266_out,
       and_267_out, and_268_out, and_269_out, and_270_out, and_271_out, and_272_out, and_273_out,
       and_274_out, and_275_out, and_276_out, and_277_out, and_278_out, and_279_out, and_280_out,
       and_281_out, and_282_out, and_283_out, and_284_out, and_285_out, and_286_out, and_287_out,
       and_288_out, and_289_out, button_1_out, button_2_out, button_3_out, button_4_out, button_5_out,
       button_6_out, button_7_out, button_8_out, button_9_out, button_10_out, button_11_out, button_12_out,
       button_13_out, button_14_out, button_15_out, button_16_out, button_17_out, button_18_out,
       button_19_out, button_20_out, button_21_out, clock_1_out, digital_oscilloscope_1_p1,
       digital_oscilloscope_1_p2, dipswitch_1_sw1, dipswitch_1_sw2, dipswitch_1_sw3, dipswitch_1_sw4,
       dipswitch_1_sw5, dipswitch_1_sw6, dipswitch_1_sw7, dipswitch_1_sw8, dipswitch_2_sw8, dipswitch_3_sw1,
       dipswitch_4_sw1, dipswitch_5_sw1, dipswitch_6_sw1, dipswitch_6_sw4, dipswitch_7_sw4, dipswitch_8_sw4,
       dipswitch_9_sw4, dipswitch_10_sw4, dipswitch_11_sw4, dipswitch_12_sw4, dipswitch_13_sw4,
       dipswitch_14_sw1, dipswitch_14_sw8, j_k_ff_1_q, j_k_ff_2_q, j_k_ff_3_q, j_k_ff_4_q, j_k_ff_5_q,
       j_k_ff_6_q, j_k_ff_7_q, j_k_ff_8_q, not_1_out, not_2_out, not_3_out, not_4_out, not_5_out, not_6_out,
       not_7_out, or_1_out, or_2_out, or_3_out, or_4_out, or_5_out, or_6_out, or_7_out, or_8_out, or_9_out,
       or_10_out, or_11_out, or_12_out, or_13_out, or_14_out, or_15_out, or_16_out, s_r_ff_1_q, s_r_ff_2_q,
       s_r_ff_3_q, s_r_ff_4_q, s_r_ff_5_q, s_r_ff_6_q, s_r_ff_7_q, s_r_ff_8_q, s_r_ff_9_q, s_r_ff_10_q,
       s_r_ff_11_q, s_r_ff_12_q, s_r_ff_13_q, s_r_ff_14_q, s_r_ff_15_q, s_r_ff_16_q, s_r_ff_17_q,
       s_r_ff_18_q, s_r_ff_19_q, s_r_ff_20_q, s_r_ff_21_q, s_r_ff_22_q, s_r_ff_23_q, s_r_ff_24_q,
       s_r_ff_25_q, s_r_ff_26_q, s_r_ff_27_q, s_r_ff_28_q, s_r_ff_29_q, s_r_ff_30_q, s_r_ff_31_q,
       s_r_ff_32_q, s_r_ff_33_q, s_r_ff_34_q, s_r_ff_35_q, s_r_ff_36_q, s_r_ff_37_q, s_r_ff_38_q,
       s_r_ff_39_q, s_r_ff_40_q, s_r_ff_41_q, s_r_ff_42_q, s_r_ff_43_q, s_r_ff_44_q, s_r_ff_45_q,
       s_r_ff_46_q, s_r_ff_47_q, s_r_ff_48_q, s_r_ff_49_q, s_r_ff_50_q, s_r_ff_51_q, s_r_ff_52_q,
       s_r_ff_53_q, s_r_ff_54_q, s_r_ff_55_q, s_r_ff_56_q, s_r_ff_57_q, s_r_ff_58_q, s_r_ff_59_q,
       s_r_ff_60_q, s_r_ff_61_q, s_r_ff_62_q, s_r_ff_63_q, s_r_ff_64_q, s_r_ff_65_q, s_r_ff_66_q,
       s_r_ff_67_q, s_r_ff_68_q, s_r_ff_69_q, s_r_ff_70_q, s_r_ff_71_q, s_r_ff_72_q, s_r_ff_73_q,
       s_r_ff_74_q, s_r_ff_75_q, s_r_ff_76_q, s_r_ff_77_q, s_r_ff_78_q, s_r_ff_79_q, s_r_ff_80_q,
       transistor_1_out, transistor_2_out, transistor_3_out, transistor_4_out, transistor_5_out,
       transistor_6_out, transistor_7_out, transistor_8_out, transistor_9_out, transistor_10_out,
       transistor_11_out, transistor_12_out, transistor_13_out, transistor_14_out, transistor_15_out,
       transistor_16_out, transistor_17_out, transistor_90_out, transistor_91_out, transistor_92_out,
       transistor_93_out, transistor_94_out, transistor_95_out, transistor_96_out, transistor_97_out,
       transistor_98_out, transistor_100_out, transistor_101_out, transistor_103_out, transistor_104_out,
       transistor_105_out, transistor_106_out, transistor_107_out, transistor_108_out, transistor_110_out,
       transistor_112_out, transistor_113_out, transistor_114_out, transistor_115_out, transistor_116_out,
       transistor_119_out, transistor_121_out, transistor_131_out, transistor_132_out, transistor_133_out,
       transistor_134_out, transistor_135_out, transistor_136_out, transistor_137_out, transistor_138_out,
       undriven, undriven_2, undriven_3, undriven_4, undriven_5, undriven_6, undriven_7, undriven_8,
       undriven_9, undriven_10, undriven_11, undriven_12, undriven_13, undriven_14, undriven_15, undriven_16,
       undriven_17, undriven_18, undriven_19, undriven_20, undriven_21, undriven_22, undriven_23,
       undriven_24, undriven_25, undriven_26, undriven_27, undriven_28, undriven_29, undriven_30,
       undriven_31, undriven_32, undriven_33, undriven_34, undriven_35, undriven_36, undriven_37,
       undriven_38, undriven_39, undriven_40, undriven_41, undriven_42, undriven_43, undriven_44,
       undriven_45, xor_1_out, xor_2_out, xor_3_out, xor_4_out, xor_5_out, xor_6_out, xor_7_out, xor_8_out,
       xor_9_out, xor_10_out, xor_11_out, xor_12_out, xor_13_out, xor_14_out, xor_15_out, xor_16_out,
       xor_17_out, xor_18_out, xor_19_out, xor_20_out, xor_21_out, xor_22_out, xor_23_out, xor_24_out,
       xor_25_out, xor_26_out, xor_27_out, xor_28_out, xor_29_out, xor_30_out, xor_31_out, xor_32_out,
       xor_33_out, xor_34_out, xor_35_out, xor_36_out, xor_37_out, xor_38_out, xor_39_out, xor_40_out,
       xor_41_out;

  and and_1 (and_1_out, transistor_1_out, dipswitch_4_sw1);
  and and_2 (and_2_out, dipswitch_4_sw1, button_4_out);
  S_R_Flip_Flop s_r_ff_1 (.Q(s_r_ff_1_q), .reset(and_2_out), .preset(and_1_out));  // open: S, R, clk, Qn
  and and_3 (and_3_out, transistor_1_out, dipswitch_5_sw1);
  and and_4 (and_4_out, dipswitch_5_sw1, button_5_out);
  S_R_Flip_Flop s_r_ff_2 (.Q(s_r_ff_2_q), .reset(and_4_out), .preset(and_3_out));  // open: S, R, clk, Qn
  xor xor_1 (xor_1_out, s_r_ff_1_q, xor_3_out);
  xor xor_2 (xor_2_out, xor_1_out, or_2_out);
  xor xor_3 (xor_3_out, dipswitch_3_sw1, s_r_ff_2_q);
  and and_5 (and_5_out, xor_1_out, or_2_out);
  or or_1 (or_1_out, and_5_out, and_6_out);
  and and_6 (and_6_out, s_r_ff_1_q, xor_3_out);
  and and_7 (and_7_out, transistor_2_out, dipswitch_4_sw1);
  and and_8 (and_8_out, dipswitch_4_sw1, button_4_out);
  and and_9 (and_9_out, transistor_2_out, dipswitch_5_sw1);
  and and_10 (and_10_out, dipswitch_5_sw1, button_5_out);
  xor xor_4 (xor_4_out, s_r_ff_3_q, xor_5_out);
  xor xor_5 (xor_5_out, dipswitch_3_sw1, s_r_ff_4_q);
  S_R_Flip_Flop s_r_ff_3 (.Q(s_r_ff_3_q), .reset(and_8_out), .preset(and_7_out));  // open: S, R, clk, Qn
  S_R_Flip_Flop s_r_ff_4 (.Q(s_r_ff_4_q), .reset(and_10_out), .preset(and_9_out));  // open: S, R, clk, Qn
  xor xor_6 (xor_6_out, xor_4_out, or_3_out);
  or or_2 (or_2_out, and_11_out, and_12_out);
  and and_11 (and_11_out, xor_4_out, or_3_out);
  and and_12 (and_12_out, s_r_ff_3_q, xor_5_out);
  xor xor_7 (xor_7_out, s_r_ff_5_q, xor_8_out);
  xor xor_8 (xor_8_out, dipswitch_3_sw1, s_r_ff_6_q);
  and and_13 (and_13_out, transistor_3_out, dipswitch_4_sw1);
  and and_14 (and_14_out, dipswitch_4_sw1, button_4_out);
  and and_15 (and_15_out, transistor_3_out, dipswitch_5_sw1);
  and and_16 (and_16_out, dipswitch_5_sw1, button_5_out);
  xor xor_9 (xor_9_out, xor_7_out, or_4_out);
  S_R_Flip_Flop s_r_ff_5 (.Q(s_r_ff_5_q), .reset(and_14_out), .preset(and_13_out));  // open: S, R, clk, Qn
  S_R_Flip_Flop s_r_ff_6 (.Q(s_r_ff_6_q), .reset(and_16_out), .preset(and_15_out));  // open: S, R, clk, Qn
  and and_17 (and_17_out, xor_7_out, or_4_out);
  or or_3 (or_3_out, and_17_out, and_18_out);
  and and_18 (and_18_out, s_r_ff_5_q, xor_8_out);
  xor xor_10 (xor_10_out, s_r_ff_7_q, xor_11_out);
  xor xor_11 (xor_11_out, dipswitch_3_sw1, s_r_ff_8_q);
  and and_19 (and_19_out, transistor_4_out, dipswitch_4_sw1);
  and and_20 (and_20_out, dipswitch_4_sw1, button_4_out);
  and and_21 (and_21_out, transistor_4_out, dipswitch_5_sw1);
  and and_22 (and_22_out, dipswitch_5_sw1, button_5_out);
  xor xor_12 (xor_12_out, xor_10_out, or_5_out);
  S_R_Flip_Flop s_r_ff_7 (.Q(s_r_ff_7_q), .reset(and_20_out), .preset(and_19_out));  // open: S, R, clk, Qn
  S_R_Flip_Flop s_r_ff_8 (.Q(s_r_ff_8_q), .reset(and_22_out), .preset(and_21_out));  // open: S, R, clk, Qn
  _7_Segment_Display u_7_segment_display_1 ();  // open: g, f, a, b, e, d, c, dp
  or or_4 (or_4_out, and_23_out, and_24_out);
  and and_23 (and_23_out, xor_10_out, or_5_out);
  and and_24 (and_24_out, s_r_ff_7_q, xor_11_out);
  // BCD_to_7_Segment_decoder bcd_to_7_segment_decoder_1: pin names not known
  xor xor_13 (xor_13_out, s_r_ff_9_q, xor_14_out);
  xor xor_14 (xor_14_out, dipswitch_3_sw1, s_r_ff_10_q);
  and and_25 (and_25_out, transistor_5_out, dipswitch_4_sw1);
  and and_26 (and_26_out, dipswitch_4_sw1, button_4_out);
  J_K_Flip_Flop j_k_ff_1 (
    .J(1'b1), .K(1'b1), .clk(j_k_ff_2_q), .Q(j_k_ff_1_q), .reset(button_2_out));  // open: Qn, preset
  xor xor_15 (xor_15_out, xor_13_out, or_6_out);
  S_R_Flip_Flop s_r_ff_9 (.Q(s_r_ff_9_q), .reset(and_26_out), .preset(and_25_out));  // open: S, R, clk, Qn
  and and_27 (and_27_out, transistor_5_out, dipswitch_5_sw1);
  and and_28 (and_28_out, dipswitch_5_sw1, button_5_out);
  or or_5 (or_5_out, and_29_out, and_30_out);
  and and_29 (and_29_out, xor_13_out, or_6_out);
  S_R_Flip_Flop s_r_ff_10 (.Q(s_r_ff_10_q), .reset(and_28_out), .preset(and_27_out));  // open: S, R, clk, Qn
  J_K_Flip_Flop j_k_ff_2 (
    .J(1'b1), .K(1'b1), .clk(j_k_ff_3_q), .Q(j_k_ff_2_q), .reset(button_2_out));  // open: Qn, preset
  and and_30 (and_30_out, s_r_ff_9_q, xor_14_out);
  xor xor_16 (xor_16_out, s_r_ff_11_q, xor_17_out);
  xor xor_17 (xor_17_out, dipswitch_3_sw1, s_r_ff_12_q);
  J_K_Flip_Flop j_k_ff_3 (
    .J(1'b1), .K(1'b1), .clk(j_k_ff_4_q), .Q(j_k_ff_3_q), .reset(button_2_out));  // open: Qn, preset
  xor xor_18 (xor_18_out, xor_16_out, or_7_out);
  and and_31 (and_31_out, xor_16_out, or_7_out);
  and and_32 (and_32_out, transistor_6_out, dipswitch_4_sw1);
  and and_33 (and_33_out, dipswitch_4_sw1, button_4_out);
  and and_34 (and_34_out, transistor_6_out, dipswitch_5_sw1);
  and and_35 (and_35_out, dipswitch_5_sw1, button_5_out);
  J_K_Flip_Flop j_k_ff_4 (
    .J(1'b1), .K(1'b1), .clk(j_k_ff_5_q), .Q(j_k_ff_4_q), .reset(button_2_out));  // open: Qn, preset
  or or_6 (or_6_out, and_31_out, and_36_out);
  and and_36 (and_36_out, s_r_ff_11_q, xor_17_out);
  S_R_Flip_Flop s_r_ff_11 (.Q(s_r_ff_11_q), .reset(and_33_out), .preset(and_32_out));  // open: S, R, clk, Qn
  S_R_Flip_Flop s_r_ff_12 (.Q(s_r_ff_12_q), .reset(and_35_out), .preset(and_34_out));  // open: S, R, clk, Qn
  J_K_Flip_Flop j_k_ff_5 (
    .J(1'b1), .K(1'b1), .clk(j_k_ff_6_q), .Q(j_k_ff_5_q), .reset(button_2_out));  // open: Qn, preset
  xor xor_19 (xor_19_out, s_r_ff_13_q, xor_20_out);
  xor xor_20 (xor_20_out, dipswitch_3_sw1, s_r_ff_14_q);
  J_K_Flip_Flop j_k_ff_6 (
    .J(1'b1), .K(1'b1), .clk(j_k_ff_7_q), .Q(j_k_ff_6_q), .reset(button_2_out));  // open: Qn, preset
  xor xor_21 (xor_21_out, xor_19_out, or_8_out);
  or or_7 (or_7_out, and_37_out, and_42_out);
  and and_37 (and_37_out, xor_19_out, or_8_out);
  and and_38 (and_38_out, transistor_7_out, dipswitch_4_sw1);
  and and_39 (and_39_out, dipswitch_4_sw1, button_4_out);
  and and_40 (and_40_out, transistor_7_out, dipswitch_5_sw1);
  and and_41 (and_41_out, dipswitch_5_sw1, button_5_out);
  J_K_Flip_Flop j_k_ff_7 (
    .J(1'b1), .K(1'b1), .clk(j_k_ff_8_q), .Q(j_k_ff_7_q), .reset(button_2_out));  // open: Qn, preset
  and and_42 (and_42_out, s_r_ff_13_q, xor_20_out);
  S_R_Flip_Flop s_r_ff_13 (.Q(s_r_ff_13_q), .reset(and_39_out), .preset(and_38_out));  // open: S, R, clk, Qn
  S_R_Flip_Flop s_r_ff_14 (.Q(s_r_ff_14_q), .reset(and_41_out), .preset(and_40_out));  // open: S, R, clk, Qn
  DipSwitch dipswitch_1 (
    .sw1(dipswitch_1_sw1), .sw2(dipswitch_1_sw2), .sw3(dipswitch_1_sw3), .sw4(dipswitch_1_sw4),
    .sw5(dipswitch_1_sw5), .sw6(dipswitch_1_sw6), .sw7(dipswitch_1_sw7), .sw8(dipswitch_1_sw8));
  Button button_1 (.out(button_1_out));
  xor xor_22 (xor_22_out, s_r_ff_15_q, xor_23_out);
  xor xor_23 (xor_23_out, dipswitch_3_sw1, s_r_ff_16_q);
  J_K_Flip_Flop j_k_ff_8 (
    .J(1'b1), .K(1'b1), .clk(digital_oscilloscope_1_p1), .Q(j_k_ff_8_q), .reset(button_2_out));  // open: Qn, preset
  xor xor_24 (xor_24_out, xor_22_out, dipswitch_3_sw1);
  Clock clock_1 (.out(clock_1_out));
  DipSwitch dipswitch_2 (.sw8(dipswitch_2_sw8));  // open: sw1, sw2, sw3, sw4, sw5, sw6, sw7
  Button button_2 (.out(button_2_out));
  // Digital_Oscilloscope digital_oscilloscope_1: pin names not known; wires that end beside it: digital_oscilloscope_1_p1, digital_oscilloscope_1_p2
  or or_8 (or_8_out, and_43_out, and_52_out);
  and and_43 (and_43_out, xor_22_out, dipswitch_3_sw1);
  and and_44 (and_44_out, dipswitch_1_sw1, button_1_out);
  and and_45 (and_45_out, dipswitch_1_sw2, button_1_out);
  and and_46 (and_46_out, dipswitch_1_sw3, button_1_out);
  and and_47 (and_47_out, dipswitch_1_sw4, button_1_out);
  and and_48 (and_48_out, dipswitch_1_sw5, button_1_out);
  and and_49 (and_49_out, dipswitch_1_sw6, button_1_out);
  and and_50 (and_50_out, dipswitch_1_sw7, button_1_out);
  and and_51 (and_51_out, dipswitch_1_sw8, button_1_out);
  LedBar ledbar_1 (
    .led0(not_1_out), .led1(not_2_out), .led2(not_3_out), .led3(not_4_out), .led4(not_5_out),
    .led5(not_6_out), .led6(not_7_out), .led7(digital_oscilloscope_1_p2));
  not not_1 (not_1_out, j_k_ff_1_q);
  not not_2 (not_2_out, j_k_ff_2_q);
  not not_3 (not_3_out, j_k_ff_3_q);
  not not_4 (not_4_out, j_k_ff_4_q);
  not not_5 (not_5_out, j_k_ff_5_q);
  not not_6 (not_6_out, j_k_ff_6_q);
  not not_7 (not_7_out, j_k_ff_7_q);
  not not_8 (digital_oscilloscope_1_p2, j_k_ff_8_q);
  // Switch switch_1: pin names not known; wires that end beside it: 1'b1, clock_1_out, digital_oscilloscope_1_p1
  and and_52 (and_52_out, s_r_ff_15_q, xor_23_out);
  and and_53 (and_53_out, transistor_8_out, dipswitch_4_sw1);
  and and_54 (and_54_out, dipswitch_4_sw1, button_4_out);
  and and_55 (and_55_out, transistor_8_out, dipswitch_5_sw1);
  and and_56 (and_56_out, dipswitch_5_sw1, button_5_out);
  S_R_Flip_Flop s_r_ff_15 (.Q(s_r_ff_15_q), .reset(and_54_out), .preset(and_53_out));  // open: S, R, clk, Qn
  S_R_Flip_Flop s_r_ff_16 (.Q(s_r_ff_16_q), .reset(and_56_out), .preset(and_55_out));  // open: S, R, clk, Qn
  and and_57 (and_57_out, xor_2_out, button_3_out);
  and and_58 (and_58_out, xor_6_out, button_3_out);
  and and_59 (and_59_out, xor_9_out, button_3_out);
  and and_60 (and_60_out, xor_12_out, button_3_out);
  and and_61 (and_61_out, xor_15_out, button_3_out);
  and and_62 (and_62_out, xor_18_out, button_3_out);
  and and_63 (and_63_out, xor_21_out, button_3_out);
  and and_64 (and_64_out, xor_24_out, button_3_out);
  and and_65 (and_65_out, not_1_out, dipswitch_2_sw8);
  and and_66 (and_66_out, not_2_out, dipswitch_2_sw8);
  and and_67 (and_67_out, not_3_out, dipswitch_2_sw8);
  and and_68 (and_68_out, not_4_out, dipswitch_2_sw8);
  and and_69 (and_69_out, not_5_out, dipswitch_2_sw8);
  and and_70 (and_70_out, not_6_out, dipswitch_2_sw8);
  and and_71 (and_71_out, not_7_out, dipswitch_2_sw8);
  and and_72 (and_72_out, digital_oscilloscope_1_p2, dipswitch_2_sw8);
  LedBar ledbar_2 (
    .led0(and_57_out), .led1(and_58_out), .led2(and_59_out), .led3(and_60_out), .led4(and_61_out),
    .led5(and_62_out), .led6(and_63_out), .led7(and_64_out));
  Button button_3 (.out(button_3_out));
  Transistor transistor_1 (.in(and_44_out), .out(transistor_1_out), .gate(1'b0));
  Transistor transistor_2 (.in(and_45_out), .out(transistor_2_out), .gate(1'b0));
  Transistor transistor_3 (.in(and_46_out), .out(transistor_3_out), .gate(1'b0));
  Transistor transistor_4 (.in(and_47_out), .out(transistor_4_out), .gate(1'b0));
  Transistor transistor_5 (.in(and_48_out), .out(transistor_5_out), .gate(1'b0));
  Transistor transistor_6 (.in(and_49_out), .out(transistor_6_out), .gate(1'b0));
  Transistor transistor_7 (.in(and_50_out), .out(transistor_7_out), .gate(1'b0));
  Transistor transistor_8 (.in(and_51_out), .out(transistor_8_out), .gate(1'b0));
  LedBar ledbar_3 (
    .led0(transistor_1_out), .led1(transistor_2_out), .led2(transistor_3_out), .led3(transistor_4_out),
    .led4(transistor_5_out), .led5(transistor_6_out), .led6(transistor_7_out), .led7(transistor_8_out));
  LedBar ledbar_4 (
    .led0(transistor_1_out), .led1(transistor_2_out), .led2(transistor_3_out), .led3(transistor_4_out),
    .led4(transistor_5_out), .led5(transistor_6_out), .led6(transistor_7_out), .led7(transistor_8_out));
  LedBar ledbar_5 (
    .led0(transistor_1_out), .led1(transistor_2_out), .led2(transistor_3_out), .led3(transistor_4_out),
    .led4(transistor_5_out), .led5(transistor_6_out), .led6(transistor_7_out), .led7(transistor_8_out));
  Transistor transistor_9 (.in(and_65_out), .out(transistor_9_out), .gate(1'b0));
  Transistor transistor_10 (.in(and_66_out), .out(transistor_10_out), .gate(1'b0));
  Transistor transistor_11 (.in(and_67_out), .out(transistor_11_out), .gate(1'b0));
  Transistor transistor_12 (.in(and_68_out), .out(transistor_12_out), .gate(1'b0));
  Transistor transistor_13 (.in(and_69_out), .out(transistor_13_out), .gate(1'b0));
  Transistor transistor_14 (.in(and_70_out), .out(transistor_14_out), .gate(1'b0));
  Transistor transistor_15 (.in(and_71_out), .out(transistor_15_out), .gate(1'b0));
  Transistor transistor_16 (.in(and_72_out), .out(transistor_16_out), .gate(1'b0));
  DipSwitch dipswitch_3 (.sw1(dipswitch_3_sw1));  // open: sw2, sw3, sw4, sw5, sw6, sw7, sw8
  DipSwitch dipswitch_4 (.sw1(dipswitch_4_sw1));  // open: sw2, sw3, sw4, sw5, sw6, sw7, sw8
  DipSwitch dipswitch_5 (.sw1(dipswitch_5_sw1));  // open: sw2, sw3, sw4, sw5, sw6, sw7, sw8
  Transistor transistor_17 (.in(or_1_out), .out(transistor_17_out), .gate(1'b0));
  Transistor transistor_18 (.in(and_57_out), .out(transistor_8_out), .gate(1'b0));
  Transistor transistor_19 (.in(and_58_out), .out(transistor_7_out), .gate(1'b0));
  Transistor transistor_20 (.in(and_59_out), .out(transistor_6_out), .gate(1'b0));
  Transistor transistor_21 (.in(and_60_out), .out(transistor_5_out), .gate(1'b0));
  Transistor transistor_22 (.in(and_61_out), .out(transistor_4_out), .gate(1'b0));
  Transistor transistor_23 (.in(and_62_out), .out(transistor_3_out), .gate(1'b0));
  Transistor transistor_24 (.in(and_63_out), .out(transistor_2_out), .gate(1'b0));
  Transistor transistor_25 (.in(and_64_out), .out(transistor_1_out), .gate(1'b0));
  Button button_4 (.out(button_4_out));
  Button button_5 (.out(button_5_out));
  LED led_1 (.in(transistor_17_out));
  LedBar ledbar_6 (
    .led0(transistor_9_out), .led1(transistor_10_out), .led2(transistor_11_out), .led3(transistor_12_out),
    .led4(transistor_13_out), .led5(transistor_14_out), .led6(transistor_15_out), .led7(transistor_16_out));
  Transistor transistor_26 (.in(and_81_out), .out(transistor_8_out), .gate(1'b0));
  Transistor transistor_27 (.in(and_82_out), .out(transistor_7_out), .gate(1'b0));
  Transistor transistor_28 (.in(and_83_out), .out(transistor_6_out), .gate(1'b0));
  Transistor transistor_29 (.in(and_84_out), .out(transistor_5_out), .gate(1'b0));
  Transistor transistor_30 (.in(and_85_out), .out(transistor_4_out), .gate(1'b0));
  Transistor transistor_31 (.in(and_86_out), .out(transistor_3_out), .gate(1'b0));
  Transistor transistor_32 (.in(and_87_out), .out(transistor_2_out), .gate(1'b0));
  Transistor transistor_33 (.in(and_88_out), .out(transistor_1_out), .gate(1'b0));
  Transistor transistor_34 (.in(and_121_out), .out(transistor_8_out), .gate(1'b0));
  Transistor transistor_35 (.in(and_122_out), .out(transistor_7_out), .gate(1'b0));
  Transistor transistor_36 (.in(and_123_out), .out(transistor_6_out), .gate(1'b0));
  Transistor transistor_37 (.in(and_124_out), .out(transistor_5_out), .gate(1'b0));
  Transistor transistor_38 (.in(and_125_out), .out(transistor_4_out), .gate(1'b0));
  Transistor transistor_39 (.in(and_126_out), .out(transistor_3_out), .gate(1'b0));
  Transistor transistor_40 (.in(and_127_out), .out(transistor_2_out), .gate(1'b0));
  Transistor transistor_41 (.in(and_128_out), .out(transistor_1_out), .gate(1'b0));
  Transistor transistor_42 (.in(and_89_out), .out(transistor_8_out), .gate(1'b0));
  Transistor transistor_43 (.in(and_90_out), .out(transistor_7_out), .gate(1'b0));
  Transistor transistor_44 (.in(and_91_out), .out(transistor_6_out), .gate(1'b0));
  Transistor transistor_45 (.in(and_92_out), .out(transistor_5_out), .gate(1'b0));
  Transistor transistor_46 (.in(and_93_out), .out(transistor_4_out), .gate(1'b0));
  Transistor transistor_47 (.in(and_94_out), .out(transistor_3_out), .gate(1'b0));
  Transistor transistor_48 (.in(and_95_out), .out(transistor_2_out), .gate(1'b0));
  Transistor transistor_49 (.in(and_96_out), .out(transistor_1_out), .gate(1'b0));
  Transistor transistor_50 (.in(and_129_out), .out(transistor_8_out), .gate(1'b0));
  Transistor transistor_51 (.in(and_130_out), .out(transistor_7_out), .gate(1'b0));
  Transistor transistor_52 (.in(and_131_out), .out(transistor_6_out), .gate(1'b0));
  Transistor transistor_53 (.in(and_132_out), .out(transistor_5_out), .gate(1'b0));
  Transistor transistor_54 (.in(and_133_out), .out(transistor_4_out), .gate(1'b0));
  Transistor transistor_55 (.in(and_134_out), .out(transistor_3_out), .gate(1'b0));
  Transistor transistor_56 (.in(and_135_out), .out(transistor_2_out), .gate(1'b0));
  Transistor transistor_57 (.in(and_136_out), .out(transistor_1_out), .gate(1'b0));
  Transistor transistor_58 (.in(and_97_out), .out(transistor_8_out), .gate(1'b0));
  Transistor transistor_59 (.in(and_98_out), .out(transistor_7_out), .gate(1'b0));
  Transistor transistor_60 (.in(and_99_out), .out(transistor_6_out), .gate(1'b0));
  Transistor transistor_61 (.in(and_100_out), .out(transistor_5_out), .gate(1'b0));
  Transistor transistor_62 (.in(and_101_out), .out(transistor_4_out), .gate(1'b0));
  Transistor transistor_63 (.in(and_102_out), .out(transistor_3_out), .gate(1'b0));
  Transistor transistor_64 (.in(and_103_out), .out(transistor_2_out), .gate(1'b0));
  Transistor transistor_65 (.in(and_104_out), .out(transistor_1_out), .gate(1'b0));
  Transistor transistor_66 (.in(and_105_out), .out(transistor_8_out), .gate(1'b0));
  Transistor transistor_67 (.in(and_106_out), .out(transistor_7_out), .gate(1'b0));
  Transistor transistor_68 (.in(and_107_out), .out(transistor_6_out), .gate(1'b0));
  Transistor transistor_69 (.in(and_108_out), .out(transistor_5_out), .gate(1'b0));
  Transistor transistor_70 (.in(and_109_out), .out(transistor_4_out), .gate(1'b0));
  Transistor transistor_71 (.in(and_110_out), .out(transistor_3_out), .gate(1'b0));
  Transistor transistor_72 (.in(and_111_out), .out(transistor_2_out), .gate(1'b0));
  Transistor transistor_73 (.in(and_112_out), .out(transistor_1_out), .gate(1'b0));
  Transistor transistor_74 (.in(and_113_out), .out(transistor_8_out), .gate(1'b0));
  Transistor transistor_75 (.in(and_114_out), .out(transistor_7_out), .gate(1'b0));
  Transistor transistor_76 (.in(and_115_out), .out(transistor_6_out), .gate(1'b0));
  Transistor transistor_77 (.in(and_116_out), .out(transistor_5_out), .gate(1'b0));
  Transistor transistor_78 (.in(and_117_out), .out(transistor_4_out), .gate(1'b0));
  Transistor transistor_79 (.in(and_118_out), .out(transistor_3_out), .gate(1'b0));
  Transistor transistor_80 (.in(and_119_out), .out(transistor_2_out), .gate(1'b0));
  Transistor transistor_81 (.in(and_120_out), .out(transistor_1_out), .gate(1'b0));
  Transistor transistor_82 (.in(and_73_out), .out(transistor_8_out), .gate(1'b0));
  Transistor transistor_83 (.in(and_74_out), .out(transistor_7_out), .gate(1'b0));
  Transistor transistor_84 (.in(and_75_out), .out(transistor_6_out), .gate(1'b0));
  Transistor transistor_85 (.in(and_76_out), .out(transistor_5_out), .gate(1'b0));
  Transistor transistor_86 (.in(and_77_out), .out(transistor_4_out), .gate(1'b0));
  Transistor transistor_87 (.in(and_78_out), .out(transistor_3_out), .gate(1'b0));
  Transistor transistor_88 (.in(and_79_out), .out(transistor_2_out), .gate(1'b0));
  Transistor transistor_89 (.in(and_80_out), .out(transistor_1_out), .gate(1'b0));
  and and_73 (and_73_out, s_r_ff_80_q, button_6_out);
  and and_74 (and_74_out, s_r_ff_72_q, button_6_out);
  and and_75 (and_75_out, s_r_ff_64_q, button_6_out);
  and and_76 (and_76_out, s_r_ff_56_q, button_6_out);
  and and_77 (and_77_out, s_r_ff_48_q, button_6_out);
  and and_78 (and_78_out, s_r_ff_40_q, button_6_out);
  and and_79 (and_79_out, s_r_ff_32_q, button_6_out);
  and and_80 (and_80_out, s_r_ff_24_q, button_6_out);
  and and_81 (and_81_out, s_r_ff_73_q, button_7_out);
  and and_82 (and_82_out, s_r_ff_65_q, button_7_out);
  and and_83 (and_83_out, s_r_ff_57_q, button_7_out);
  and and_84 (and_84_out, s_r_ff_49_q, button_7_out);
  and and_85 (and_85_out, s_r_ff_41_q, button_7_out);
  and and_86 (and_86_out, s_r_ff_33_q, button_7_out);
  and and_87 (and_87_out, s_r_ff_25_q, button_7_out);
  and and_88 (and_88_out, s_r_ff_17_q, button_7_out);
  and and_89 (and_89_out, s_r_ff_75_q, button_10_out);
  and and_90 (and_90_out, s_r_ff_67_q, button_10_out);
  and and_91 (and_91_out, s_r_ff_59_q, button_10_out);
  and and_92 (and_92_out, s_r_ff_51_q, button_10_out);
  and and_93 (and_93_out, s_r_ff_43_q, button_10_out);
  and and_94 (and_94_out, s_r_ff_35_q, button_10_out);
  and and_95 (and_95_out, s_r_ff_27_q, button_10_out);
  and and_96 (and_96_out, s_r_ff_19_q, button_10_out);
  and and_97 (and_97_out, s_r_ff_77_q, button_12_out);
  and and_98 (and_98_out, s_r_ff_69_q, button_12_out);
  and and_99 (and_99_out, s_r_ff_61_q, button_12_out);
  and and_100 (and_100_out, s_r_ff_53_q, button_12_out);
  and and_101 (and_101_out, s_r_ff_45_q, button_12_out);
  and and_102 (and_102_out, s_r_ff_37_q, button_12_out);
  and and_103 (and_103_out, s_r_ff_29_q, button_12_out);
  and and_104 (and_104_out, s_r_ff_21_q, button_12_out);
  and and_105 (and_105_out, s_r_ff_78_q, button_9_out);
  and and_106 (and_106_out, s_r_ff_70_q, button_9_out);
  and and_107 (and_107_out, s_r_ff_62_q, button_9_out);
  and and_108 (and_108_out, s_r_ff_54_q, button_9_out);
  and and_109 (and_109_out, s_r_ff_46_q, button_9_out);
  and and_110 (and_110_out, s_r_ff_38_q, button_9_out);
  and and_111 (and_111_out, s_r_ff_30_q, button_9_out);
  and and_112 (and_112_out, s_r_ff_22_q, button_9_out);
  and and_113 (and_113_out, s_r_ff_79_q, button_13_out);
  and and_114 (and_114_out, s_r_ff_71_q, button_13_out);
  and and_115 (and_115_out, s_r_ff_63_q, button_13_out);
  and and_116 (and_116_out, s_r_ff_55_q, button_13_out);
  and and_117 (and_117_out, s_r_ff_47_q, button_13_out);
  and and_118 (and_118_out, s_r_ff_39_q, button_13_out);
  and and_119 (and_119_out, s_r_ff_31_q, button_13_out);
  and and_120 (and_120_out, s_r_ff_23_q, button_13_out);
  and and_121 (and_121_out, s_r_ff_74_q, button_8_out);
  and and_122 (and_122_out, s_r_ff_66_q, button_8_out);
  and and_123 (and_123_out, s_r_ff_58_q, button_8_out);
  and and_124 (and_124_out, s_r_ff_50_q, button_8_out);
  and and_125 (and_125_out, s_r_ff_42_q, button_8_out);
  and and_126 (and_126_out, s_r_ff_34_q, button_8_out);
  and and_127 (and_127_out, s_r_ff_26_q, button_8_out);
  and and_128 (and_128_out, s_r_ff_18_q, button_8_out);
  and and_129 (and_129_out, s_r_ff_76_q, button_11_out);
  and and_130 (and_130_out, s_r_ff_68_q, button_11_out);
  and and_131 (and_131_out, s_r_ff_60_q, button_11_out);
  and and_132 (and_132_out, s_r_ff_52_q, button_11_out);
  and and_133 (and_133_out, s_r_ff_44_q, button_11_out);
  and and_134 (and_134_out, s_r_ff_36_q, button_11_out);
  and and_135 (and_135_out, s_r_ff_28_q, button_11_out);
  and and_136 (and_136_out, s_r_ff_20_q, button_11_out);
  and and_137 (and_137_out, undriven_11, undriven);
  LedBar ledbar_7 (
    .led0(s_r_ff_17_q), .led1(s_r_ff_25_q), .led2(s_r_ff_33_q), .led3(s_r_ff_41_q), .led4(s_r_ff_49_q),
    .led5(s_r_ff_57_q), .led6(s_r_ff_65_q), .led7(s_r_ff_73_q));
  LedBar ledbar_8 (
    .led0(s_r_ff_18_q), .led1(s_r_ff_26_q), .led2(s_r_ff_34_q), .led3(s_r_ff_42_q), .led4(s_r_ff_50_q),
    .led5(s_r_ff_58_q), .led6(s_r_ff_66_q), .led7(s_r_ff_74_q));
  LedBar ledbar_9 (
    .led0(s_r_ff_19_q), .led1(s_r_ff_27_q), .led2(s_r_ff_35_q), .led3(s_r_ff_43_q), .led4(s_r_ff_51_q),
    .led5(s_r_ff_59_q), .led6(s_r_ff_67_q), .led7(s_r_ff_75_q));
  LedBar ledbar_10 (
    .led0(s_r_ff_20_q), .led1(s_r_ff_28_q), .led2(s_r_ff_36_q), .led3(s_r_ff_44_q), .led4(s_r_ff_52_q),
    .led5(s_r_ff_60_q), .led6(s_r_ff_68_q), .led7(s_r_ff_76_q));
  LedBar ledbar_11 (
    .led0(s_r_ff_21_q), .led1(s_r_ff_29_q), .led2(s_r_ff_37_q), .led3(s_r_ff_45_q), .led4(s_r_ff_53_q),
    .led5(s_r_ff_61_q), .led6(s_r_ff_69_q), .led7(s_r_ff_77_q));
  LedBar ledbar_12 (
    .led0(s_r_ff_22_q), .led1(s_r_ff_30_q), .led2(s_r_ff_38_q), .led3(s_r_ff_46_q), .led4(s_r_ff_54_q),
    .led5(s_r_ff_62_q), .led6(s_r_ff_70_q), .led7(s_r_ff_78_q));
  LedBar ledbar_13 (
    .led0(s_r_ff_23_q), .led1(s_r_ff_31_q), .led2(s_r_ff_39_q), .led3(s_r_ff_47_q), .led4(s_r_ff_55_q),
    .led5(s_r_ff_63_q), .led6(s_r_ff_71_q), .led7(s_r_ff_79_q));
  LedBar ledbar_14 (
    .led0(s_r_ff_24_q), .led1(s_r_ff_32_q), .led2(s_r_ff_40_q), .led3(s_r_ff_48_q), .led4(s_r_ff_56_q),
    .led5(s_r_ff_64_q), .led6(s_r_ff_72_q), .led7(s_r_ff_80_q));
  xor xor_25 (xor_25_out, undriven_6, undriven_7);
  and and_138 (and_138_out, undriven_11, undriven_2);
  xor xor_26 (xor_26_out, xor_25_out, undriven_5);
  and and_139 (and_139_out, undriven_11, undriven_3);
  and and_140 (and_140_out, xor_25_out, undriven_5);
  and and_141 (and_141_out, undriven_11, undriven_4);
  or or_9 (or_9_out, and_140_out, and_142_out);
  and and_142 (and_142_out, undriven_6, undriven_7);
  and and_143 (and_143_out, undriven_11, undriven_8);
  and and_144 (and_144_out, transistor_1_out, transistor_90_out);
  and and_145 (and_145_out, transistor_90_out, transistor_98_out);
  and and_146 (and_146_out, transistor_1_out, transistor_101_out);
  and and_147 (and_147_out, transistor_101_out, transistor_100_out);
  and and_148 (and_148_out, transistor_1_out, transistor_104_out);
  and and_149 (and_149_out, transistor_104_out, transistor_103_out);
  and and_150 (and_150_out, transistor_1_out, transistor_106_out);
  and and_151 (and_151_out, transistor_106_out, transistor_105_out);
  and and_152 (and_152_out, transistor_1_out, transistor_107_out);
  and and_153 (and_153_out, transistor_107_out, transistor_119_out);
  and and_154 (and_154_out, transistor_1_out, transistor_91_out);
  and and_155 (and_155_out, transistor_91_out, transistor_108_out);
  and and_156 (and_156_out, transistor_1_out, transistor_110_out);
  and and_157 (and_157_out, transistor_110_out, transistor_121_out);
  and and_158 (and_158_out, transistor_1_out, transistor_93_out);
  and and_159 (and_159_out, transistor_93_out, transistor_92_out);
  and and_160 (and_160_out, undriven_11, undriven_9);
  S_R_Flip_Flop s_r_ff_17 (.Q(s_r_ff_17_q), .reset(and_145_out), .preset(and_144_out));  // open: S, R, clk, Qn
  S_R_Flip_Flop s_r_ff_18 (.Q(s_r_ff_18_q), .reset(and_147_out), .preset(and_146_out));  // open: S, R, clk, Qn
  S_R_Flip_Flop s_r_ff_19 (.Q(s_r_ff_19_q), .reset(and_149_out), .preset(and_148_out));  // open: S, R, clk, Qn
  S_R_Flip_Flop s_r_ff_20 (.Q(s_r_ff_20_q), .reset(and_151_out), .preset(and_150_out));  // open: S, R, clk, Qn
  S_R_Flip_Flop s_r_ff_21 (.Q(s_r_ff_21_q), .reset(and_153_out), .preset(and_152_out));  // open: S, R, clk, Qn
  S_R_Flip_Flop s_r_ff_22 (.Q(s_r_ff_22_q), .reset(and_155_out), .preset(and_154_out));  // open: S, R, clk, Qn
  S_R_Flip_Flop s_r_ff_23 (.Q(s_r_ff_23_q), .reset(and_157_out), .preset(and_156_out));  // open: S, R, clk, Qn
  S_R_Flip_Flop s_r_ff_24 (.Q(s_r_ff_24_q), .reset(and_159_out), .preset(and_158_out));  // open: S, R, clk, Qn
  and and_161 (and_161_out, undriven_11, undriven_10);
  and and_162 (and_162_out, undriven_11, undriven_12);
  xor xor_27 (xor_27_out, undriven_13, undriven_14);
  and and_163 (and_163_out, transistor_2_out, transistor_90_out);
  and and_164 (and_164_out, transistor_90_out, transistor_98_out);
  and and_165 (and_165_out, transistor_2_out, transistor_101_out);
  and and_166 (and_166_out, transistor_101_out, transistor_100_out);
  and and_167 (and_167_out, transistor_2_out, transistor_104_out);
  and and_168 (and_168_out, transistor_104_out, transistor_103_out);
  and and_169 (and_169_out, transistor_2_out, transistor_106_out);
  and and_170 (and_170_out, transistor_106_out, transistor_105_out);
  and and_171 (and_171_out, transistor_2_out, transistor_107_out);
  and and_172 (and_172_out, transistor_107_out, transistor_119_out);
  and and_173 (and_173_out, transistor_2_out, transistor_91_out);
  and and_174 (and_174_out, transistor_91_out, transistor_108_out);
  and and_175 (and_175_out, transistor_2_out, transistor_110_out);
  and and_176 (and_176_out, transistor_110_out, transistor_121_out);
  and and_177 (and_177_out, transistor_2_out, transistor_93_out);
  and and_178 (and_178_out, transistor_93_out, transistor_92_out);
  xor xor_28 (xor_28_out, xor_27_out, or_11_out);
  S_R_Flip_Flop s_r_ff_25 (.Q(s_r_ff_25_q), .reset(and_164_out), .preset(and_163_out));  // open: S, R, clk, Qn
  S_R_Flip_Flop s_r_ff_26 (.Q(s_r_ff_26_q), .reset(and_166_out), .preset(and_165_out));  // open: S, R, clk, Qn
  S_R_Flip_Flop s_r_ff_27 (.Q(s_r_ff_27_q), .reset(and_168_out), .preset(and_167_out));  // open: S, R, clk, Qn
  S_R_Flip_Flop s_r_ff_28 (.Q(s_r_ff_28_q), .reset(and_170_out), .preset(and_169_out));  // open: S, R, clk, Qn
  S_R_Flip_Flop s_r_ff_29 (.Q(s_r_ff_29_q), .reset(and_172_out), .preset(and_171_out));  // open: S, R, clk, Qn
  S_R_Flip_Flop s_r_ff_30 (.Q(s_r_ff_30_q), .reset(and_174_out), .preset(and_173_out));  // open: S, R, clk, Qn
  S_R_Flip_Flop s_r_ff_31 (.Q(s_r_ff_31_q), .reset(and_176_out), .preset(and_175_out));  // open: S, R, clk, Qn
  S_R_Flip_Flop s_r_ff_32 (.Q(s_r_ff_32_q), .reset(and_178_out), .preset(and_177_out));  // open: S, R, clk, Qn
  or or_10 (or_10_out, and_179_out, and_180_out);
  and and_179 (and_179_out, xor_27_out, or_11_out);
  and and_180 (and_180_out, undriven_13, undriven_14);
  xor xor_29 (xor_29_out, undriven_15, undriven_16);
  xor xor_30 (xor_30_out, xor_29_out, or_12_out);
  and and_181 (and_181_out, transistor_3_out, transistor_90_out);
  and and_182 (and_182_out, transistor_90_out, transistor_98_out);
  and and_183 (and_183_out, transistor_3_out, transistor_101_out);
  and and_184 (and_184_out, transistor_101_out, transistor_100_out);
  and and_185 (and_185_out, transistor_3_out, transistor_104_out);
  and and_186 (and_186_out, transistor_104_out, transistor_103_out);
  and and_187 (and_187_out, transistor_3_out, transistor_106_out);
  and and_188 (and_188_out, transistor_106_out, transistor_105_out);
  and and_189 (and_189_out, transistor_3_out, transistor_107_out);
  and and_190 (and_190_out, transistor_107_out, transistor_119_out);
  and and_191 (and_191_out, transistor_3_out, transistor_91_out);
  and and_192 (and_192_out, transistor_91_out, transistor_108_out);
  and and_193 (and_193_out, transistor_3_out, transistor_110_out);
  and and_194 (and_194_out, transistor_110_out, transistor_121_out);
  and and_195 (and_195_out, transistor_3_out, transistor_93_out);
  and and_196 (and_196_out, transistor_93_out, transistor_92_out);
  or or_11 (or_11_out, and_197_out, and_198_out);
  and and_197 (and_197_out, xor_29_out, or_12_out);
  S_R_Flip_Flop s_r_ff_33 (.Q(s_r_ff_33_q), .reset(and_182_out), .preset(and_181_out));  // open: S, R, clk, Qn
  S_R_Flip_Flop s_r_ff_34 (.Q(s_r_ff_34_q), .reset(and_184_out), .preset(and_183_out));  // open: S, R, clk, Qn
  S_R_Flip_Flop s_r_ff_35 (.Q(s_r_ff_35_q), .reset(and_186_out), .preset(and_185_out));  // open: S, R, clk, Qn
  S_R_Flip_Flop s_r_ff_36 (.Q(s_r_ff_36_q), .reset(and_188_out), .preset(and_187_out));  // open: S, R, clk, Qn
  S_R_Flip_Flop s_r_ff_37 (.Q(s_r_ff_37_q), .reset(and_190_out), .preset(and_189_out));  // open: S, R, clk, Qn
  S_R_Flip_Flop s_r_ff_38 (.Q(s_r_ff_38_q), .reset(and_192_out), .preset(and_191_out));  // open: S, R, clk, Qn
  S_R_Flip_Flop s_r_ff_39 (.Q(s_r_ff_39_q), .reset(and_194_out), .preset(and_193_out));  // open: S, R, clk, Qn
  S_R_Flip_Flop s_r_ff_40 (.Q(s_r_ff_40_q), .reset(and_196_out), .preset(and_195_out));  // open: S, R, clk, Qn
  and and_198 (and_198_out, undriven_15, undriven_16);
  xor xor_31 (xor_31_out, undriven_17, undriven_18);
  xor xor_32 (xor_32_out, xor_31_out, or_13_out);
  and and_199 (and_199_out, transistor_4_out, transistor_90_out);
  and and_200 (and_200_out, transistor_90_out, transistor_98_out);
  and and_201 (and_201_out, transistor_4_out, transistor_101_out);
  and and_202 (and_202_out, transistor_101_out, transistor_100_out);
  and and_203 (and_203_out, transistor_4_out, transistor_104_out);
  and and_204 (and_204_out, transistor_104_out, transistor_103_out);
  and and_205 (and_205_out, transistor_4_out, transistor_106_out);
  and and_206 (and_206_out, transistor_106_out, transistor_105_out);
  and and_207 (and_207_out, transistor_4_out, transistor_107_out);
  and and_208 (and_208_out, transistor_107_out, transistor_119_out);
  and and_209 (and_209_out, transistor_4_out, transistor_91_out);
  and and_210 (and_210_out, transistor_91_out, transistor_108_out);
  and and_211 (and_211_out, transistor_4_out, transistor_110_out);
  and and_212 (and_212_out, transistor_110_out, transistor_121_out);
  and and_213 (and_213_out, transistor_4_out, transistor_93_out);
  and and_214 (and_214_out, transistor_93_out, transistor_92_out);
  or or_12 (or_12_out, and_215_out, and_216_out);
  and and_215 (and_215_out, xor_31_out, or_13_out);
  S_R_Flip_Flop s_r_ff_41 (.Q(s_r_ff_41_q), .reset(and_200_out), .preset(and_199_out));  // open: S, R, clk, Qn
  S_R_Flip_Flop s_r_ff_42 (.Q(s_r_ff_42_q), .reset(and_202_out), .preset(and_201_out));  // open: S, R, clk, Qn
  S_R_Flip_Flop s_r_ff_43 (.Q(s_r_ff_43_q), .reset(and_204_out), .preset(and_203_out));  // open: S, R, clk, Qn
  S_R_Flip_Flop s_r_ff_44 (.Q(s_r_ff_44_q), .reset(and_206_out), .preset(and_205_out));  // open: S, R, clk, Qn
  S_R_Flip_Flop s_r_ff_45 (.Q(s_r_ff_45_q), .reset(and_208_out), .preset(and_207_out));  // open: S, R, clk, Qn
  S_R_Flip_Flop s_r_ff_46 (.Q(s_r_ff_46_q), .reset(and_210_out), .preset(and_209_out));  // open: S, R, clk, Qn
  S_R_Flip_Flop s_r_ff_47 (.Q(s_r_ff_47_q), .reset(and_212_out), .preset(and_211_out));  // open: S, R, clk, Qn
  S_R_Flip_Flop s_r_ff_48 (.Q(s_r_ff_48_q), .reset(and_214_out), .preset(and_213_out));  // open: S, R, clk, Qn
  and and_216 (and_216_out, undriven_17, undriven_18);
  xor xor_33 (xor_33_out, undriven_19, undriven_20);
  xor xor_34 (xor_34_out, xor_33_out, or_14_out);
  or or_13 (or_13_out, and_217_out, and_234_out);
  and and_217 (and_217_out, xor_33_out, or_14_out);
  and and_218 (and_218_out, transistor_5_out, transistor_90_out);
  and and_219 (and_219_out, transistor_90_out, transistor_98_out);
  and and_220 (and_220_out, transistor_5_out, transistor_101_out);
  and and_221 (and_221_out, transistor_101_out, transistor_100_out);
  and and_222 (and_222_out, transistor_5_out, transistor_104_out);
  and and_223 (and_223_out, transistor_104_out, transistor_103_out);
  and and_224 (and_224_out, transistor_5_out, transistor_106_out);
  and and_225 (and_225_out, transistor_106_out, transistor_105_out);
  and and_226 (and_226_out, transistor_5_out, transistor_107_out);
  and and_227 (and_227_out, transistor_107_out, transistor_119_out);
  and and_228 (and_228_out, transistor_5_out, transistor_91_out);
  and and_229 (and_229_out, transistor_91_out, transistor_108_out);
  and and_230 (and_230_out, transistor_5_out, transistor_110_out);
  and and_231 (and_231_out, transistor_110_out, transistor_121_out);
  and and_232 (and_232_out, transistor_5_out, transistor_93_out);
  and and_233 (and_233_out, transistor_93_out, transistor_92_out);
  and and_234 (and_234_out, undriven_19, undriven_20);
  S_R_Flip_Flop s_r_ff_49 (.Q(s_r_ff_49_q), .reset(and_219_out), .preset(and_218_out));  // open: S, R, clk, Qn
  S_R_Flip_Flop s_r_ff_50 (.Q(s_r_ff_50_q), .reset(and_221_out), .preset(and_220_out));  // open: S, R, clk, Qn
  S_R_Flip_Flop s_r_ff_51 (.Q(s_r_ff_51_q), .reset(and_223_out), .preset(and_222_out));  // open: S, R, clk, Qn
  S_R_Flip_Flop s_r_ff_52 (.Q(s_r_ff_52_q), .reset(and_225_out), .preset(and_224_out));  // open: S, R, clk, Qn
  S_R_Flip_Flop s_r_ff_53 (.Q(s_r_ff_53_q), .reset(and_227_out), .preset(and_226_out));  // open: S, R, clk, Qn
  S_R_Flip_Flop s_r_ff_54 (.Q(s_r_ff_54_q), .reset(and_229_out), .preset(and_228_out));  // open: S, R, clk, Qn
  S_R_Flip_Flop s_r_ff_55 (.Q(s_r_ff_55_q), .reset(and_231_out), .preset(and_230_out));  // open: S, R, clk, Qn
  S_R_Flip_Flop s_r_ff_56 (.Q(s_r_ff_56_q), .reset(and_233_out), .preset(and_232_out));  // open: S, R, clk, Qn
  xor xor_35 (xor_35_out, undriven_21, undriven_22);
  xor xor_36 (xor_36_out, xor_35_out, or_15_out);
  or or_14 (or_14_out, and_235_out, and_236_out);
  and and_235 (and_235_out, xor_35_out, or_15_out);
  and and_236 (and_236_out, undriven_21, undriven_22);
  xor xor_37 (xor_37_out, undriven_23, undriven_24);
  and and_237 (and_237_out, transistor_6_out, transistor_90_out);
  and and_238 (and_238_out, transistor_90_out, transistor_98_out);
  and and_239 (and_239_out, transistor_6_out, transistor_101_out);
  and and_240 (and_240_out, transistor_101_out, transistor_100_out);
  and and_241 (and_241_out, transistor_6_out, transistor_104_out);
  and and_242 (and_242_out, transistor_104_out, transistor_103_out);
  and and_243 (and_243_out, transistor_6_out, transistor_106_out);
  and and_244 (and_244_out, transistor_106_out, transistor_105_out);
  and and_245 (and_245_out, transistor_6_out, transistor_107_out);
  and and_246 (and_246_out, transistor_107_out, transistor_119_out);
  and and_247 (and_247_out, transistor_6_out, transistor_91_out);
  and and_248 (and_248_out, transistor_91_out, transistor_108_out);
  and and_249 (and_249_out, transistor_6_out, transistor_110_out);
  and and_250 (and_250_out, transistor_110_out, transistor_121_out);
  and and_251 (and_251_out, transistor_6_out, transistor_93_out);
  and and_252 (and_252_out, transistor_93_out, transistor_92_out);
  xor xor_38 (xor_38_out, xor_37_out, or_16_out);
  S_R_Flip_Flop s_r_ff_57 (.Q(s_r_ff_57_q), .reset(and_238_out), .preset(and_237_out));  // open: S, R, clk, Qn
  S_R_Flip_Flop s_r_ff_58 (.Q(s_r_ff_58_q), .reset(and_240_out), .preset(and_239_out));  // open: S, R, clk, Qn
  S_R_Flip_Flop s_r_ff_59 (.Q(s_r_ff_59_q), .reset(and_242_out), .preset(and_241_out));  // open: S, R, clk, Qn
  S_R_Flip_Flop s_r_ff_60 (.Q(s_r_ff_60_q), .reset(and_244_out), .preset(and_243_out));  // open: S, R, clk, Qn
  S_R_Flip_Flop s_r_ff_61 (.Q(s_r_ff_61_q), .reset(and_246_out), .preset(and_245_out));  // open: S, R, clk, Qn
  S_R_Flip_Flop s_r_ff_62 (.Q(s_r_ff_62_q), .reset(and_248_out), .preset(and_247_out));  // open: S, R, clk, Qn
  S_R_Flip_Flop s_r_ff_63 (.Q(s_r_ff_63_q), .reset(and_250_out), .preset(and_249_out));  // open: S, R, clk, Qn
  S_R_Flip_Flop s_r_ff_64 (.Q(s_r_ff_64_q), .reset(and_252_out), .preset(and_251_out));  // open: S, R, clk, Qn
  or or_15 (or_15_out, and_253_out, and_254_out);
  and and_253 (and_253_out, xor_37_out, or_16_out);
  and and_254 (and_254_out, undriven_23, undriven_24);
  xor xor_39 (xor_39_out, undriven_25, undriven_26);
  xor xor_40 (xor_40_out, xor_39_out, and_289_out);
  and and_255 (and_255_out, transistor_7_out, transistor_90_out);
  and and_256 (and_256_out, transistor_90_out, transistor_98_out);
  and and_257 (and_257_out, transistor_7_out, transistor_101_out);
  and and_258 (and_258_out, transistor_101_out, transistor_100_out);
  and and_259 (and_259_out, transistor_7_out, transistor_104_out);
  and and_260 (and_260_out, transistor_104_out, transistor_103_out);
  and and_261 (and_261_out, transistor_7_out, transistor_106_out);
  and and_262 (and_262_out, transistor_106_out, transistor_105_out);
  and and_263 (and_263_out, transistor_7_out, transistor_107_out);
  and and_264 (and_264_out, transistor_107_out, transistor_119_out);
  and and_265 (and_265_out, transistor_7_out, transistor_91_out);
  and and_266 (and_266_out, transistor_91_out, transistor_108_out);
  and and_267 (and_267_out, transistor_7_out, transistor_110_out);
  and and_268 (and_268_out, transistor_110_out, transistor_121_out);
  and and_269 (and_269_out, transistor_7_out, transistor_93_out);
  and and_270 (and_270_out, transistor_93_out, transistor_92_out);
  and and_271 (and_271_out, xor_39_out, and_289_out);
  S_R_Flip_Flop s_r_ff_65 (.Q(s_r_ff_65_q), .reset(and_256_out), .preset(and_255_out));  // open: S, R, clk, Qn
  S_R_Flip_Flop s_r_ff_66 (.Q(s_r_ff_66_q), .reset(and_258_out), .preset(and_257_out));  // open: S, R, clk, Qn
  S_R_Flip_Flop s_r_ff_67 (.Q(s_r_ff_67_q), .reset(and_260_out), .preset(and_259_out));  // open: S, R, clk, Qn
  S_R_Flip_Flop s_r_ff_68 (.Q(s_r_ff_68_q), .reset(and_262_out), .preset(and_261_out));  // open: S, R, clk, Qn
  S_R_Flip_Flop s_r_ff_69 (.Q(s_r_ff_69_q), .reset(and_264_out), .preset(and_263_out));  // open: S, R, clk, Qn
  S_R_Flip_Flop s_r_ff_70 (.Q(s_r_ff_70_q), .reset(and_266_out), .preset(and_265_out));  // open: S, R, clk, Qn
  S_R_Flip_Flop s_r_ff_71 (.Q(s_r_ff_71_q), .reset(and_268_out), .preset(and_267_out));  // open: S, R, clk, Qn
  S_R_Flip_Flop s_r_ff_72 (.Q(s_r_ff_72_q), .reset(and_270_out), .preset(and_269_out));  // open: S, R, clk, Qn
  or or_16 (or_16_out, and_271_out, and_272_out);
  and and_272 (and_272_out, undriven_25, undriven_26);
  xor xor_41 (xor_41_out, undriven_27, undriven_28);
  and and_273 (and_273_out, transistor_8_out, transistor_90_out);
  and and_274 (and_274_out, transistor_90_out, transistor_98_out);
  and and_275 (and_275_out, transistor_8_out, transistor_101_out);
  and and_276 (and_276_out, transistor_101_out, transistor_100_out);
  and and_277 (and_277_out, transistor_8_out, transistor_104_out);
  and and_278 (and_278_out, transistor_104_out, transistor_103_out);
  and and_279 (and_279_out, transistor_8_out, transistor_106_out);
  and and_280 (and_280_out, transistor_106_out, transistor_105_out);
  and and_281 (and_281_out, transistor_8_out, transistor_107_out);
  and and_282 (and_282_out, transistor_107_out, transistor_119_out);
  and and_283 (and_283_out, transistor_8_out, transistor_91_out);
  and and_284 (and_284_out, transistor_91_out, transistor_108_out);
  and and_285 (and_285_out, transistor_8_out, transistor_110_out);
  and and_286 (and_286_out, transistor_110_out, transistor_121_out);
  and and_287 (and_287_out, transistor_8_out, transistor_93_out);
  and and_288 (and_288_out, transistor_93_out, transistor_92_out);
  and and_289 (and_289_out, undriven_27, undriven_28);
  S_R_Flip_Flop s_r_ff_73 (.Q(s_r_ff_73_q), .reset(and_274_out), .preset(and_273_out));  // open: S, R, clk, Qn
  S_R_Flip_Flop s_r_ff_74 (.Q(s_r_ff_74_q), .reset(and_276_out), .preset(and_275_out));  // open: S, R, clk, Qn
  S_R_Flip_Flop s_r_ff_75 (.Q(s_r_ff_75_q), .reset(and_278_out), .preset(and_277_out));  // open: S, R, clk, Qn
  S_R_Flip_Flop s_r_ff_76 (.Q(s_r_ff_76_q), .reset(and_280_out), .preset(and_279_out));  // open: S, R, clk, Qn
  S_R_Flip_Flop s_r_ff_77 (.Q(s_r_ff_77_q), .reset(and_282_out), .preset(and_281_out));  // open: S, R, clk, Qn
  S_R_Flip_Flop s_r_ff_78 (.Q(s_r_ff_78_q), .reset(and_284_out), .preset(and_283_out));  // open: S, R, clk, Qn
  S_R_Flip_Flop s_r_ff_79 (.Q(s_r_ff_79_q), .reset(and_286_out), .preset(and_285_out));  // open: S, R, clk, Qn
  S_R_Flip_Flop s_r_ff_80 (.Q(s_r_ff_80_q), .reset(and_288_out), .preset(and_287_out));  // open: S, R, clk, Qn
  Button button_6 (.out(button_6_out));
  DipSwitch dipswitch_6 (.sw1(dipswitch_6_sw1), .sw4(dipswitch_6_sw4));  // open: sw2, sw3, sw5, sw6, sw7, sw8
  Button button_7 (.out(button_7_out));
  Button button_8 (.out(button_8_out));
  DipSwitch dipswitch_7 (.sw4(dipswitch_7_sw4));  // open: sw1, sw2, sw3, sw5, sw6, sw7, sw8
  Button button_9 (.out(button_9_out));
  DipSwitch dipswitch_8 (.sw4(dipswitch_8_sw4));  // open: sw1, sw2, sw3, sw5, sw6, sw7, sw8
  Transistor transistor_90 (.in(dipswitch_6_sw4), .out(transistor_90_out), .gate(1'b0));
  DipSwitch dipswitch_9 (.sw4(dipswitch_9_sw4));  // open: sw1, sw2, sw3, sw5, sw6, sw7, sw8
  DipSwitch dipswitch_10 (.sw4(dipswitch_10_sw4));  // open: sw1, sw2, sw3, sw5, sw6, sw7, sw8
  Button button_10 (.out(button_10_out));
  DipSwitch dipswitch_11 (.sw4(dipswitch_11_sw4));  // open: sw1, sw2, sw3, sw5, sw6, sw7, sw8
  Button button_11 (.out(button_11_out));
  DipSwitch dipswitch_12 (.sw4(dipswitch_12_sw4));  // open: sw1, sw2, sw3, sw5, sw6, sw7, sw8
  Button button_12 (.out(button_12_out));
  Transistor transistor_91 (.in(dipswitch_7_sw4), .out(transistor_91_out), .gate(1'b0));
  DipSwitch dipswitch_13 (.sw4(dipswitch_13_sw4));  // open: sw1, sw2, sw3, sw5, sw6, sw7, sw8
  Button button_13 (.out(button_13_out));
  Transistor transistor_92 (.in(dipswitch_14_sw1), .out(transistor_92_out), .gate(1'b0));
  Transistor transistor_93 (.in(dipswitch_8_sw4), .out(transistor_93_out), .gate(1'b0));
  Transistor transistor_94 (.in(undriven_31), .out(transistor_94_out), .gate(1'b0));
  Transistor transistor_95 (.in(undriven_33), .out(transistor_95_out), .gate(1'b0));
  Transistor transistor_96 (.in(undriven_34), .out(transistor_96_out), .gate(1'b0));
  Transistor transistor_97 (.in(undriven_36), .out(transistor_97_out), .gate(1'b0));
  Transistor transistor_98 (.in(dipswitch_14_sw1), .out(transistor_98_out), .gate(1'b0));
  Transistor transistor_99 (.in(button_14_out), .out(transistor_98_out), .gate(1'b0));
  Button button_14 (.out(button_14_out));
  Transistor transistor_100 (.in(dipswitch_14_sw1), .out(transistor_100_out), .gate(1'b0));
  Transistor transistor_101 (.in(dipswitch_9_sw4), .out(transistor_101_out), .gate(1'b0));
  Transistor transistor_102 (.in(button_15_out), .out(transistor_100_out), .gate(1'b0));
  Button button_15 (.out(button_15_out));
  Transistor transistor_103 (.in(dipswitch_14_sw1), .out(transistor_103_out), .gate(1'b0));
  Transistor transistor_104 (.in(dipswitch_10_sw4), .out(transistor_104_out), .gate(1'b0));
  Transistor transistor_105 (.in(dipswitch_14_sw1), .out(transistor_105_out), .gate(1'b0));
  Transistor transistor_106 (.in(dipswitch_11_sw4), .out(transistor_106_out), .gate(1'b0));
  Transistor transistor_107 (.in(dipswitch_12_sw4), .out(transistor_107_out), .gate(1'b0));
  Transistor transistor_108 (.in(dipswitch_14_sw1), .out(transistor_108_out), .gate(1'b0));
  Transistor transistor_109 (.in(button_16_out), .out(transistor_108_out), .gate(1'b0));
  Button button_16 (.out(button_16_out));
  Transistor transistor_110 (.in(dipswitch_13_sw4), .out(transistor_110_out), .gate(1'b0));
  Transistor transistor_111 (.in(button_17_out), .out(transistor_92_out), .gate(1'b0));
  Button button_17 (.out(button_17_out));
  Transistor transistor_112 (.in(undriven_37), .out(transistor_112_out), .gate(1'b0));
  Transistor transistor_113 (.in(undriven_35), .out(transistor_113_out), .gate(1'b0));
  Transistor transistor_114 (.in(undriven_32), .out(transistor_114_out), .gate(1'b0));
  Transistor transistor_115 (.in(undriven_30), .out(transistor_115_out), .gate(1'b0));
  Transistor transistor_116 (.in(undriven_29), .out(transistor_116_out), .gate(1'b0));
  Transistor transistor_117 (.in(button_18_out), .out(transistor_103_out), .gate(1'b0));
  Button button_18 (.out(button_18_out));
  Transistor transistor_118 (.in(button_19_out), .out(transistor_105_out), .gate(1'b0));
  Button button_19 (.out(button_19_out));
  Transistor transistor_119 (.in(dipswitch_14_sw1), .out(transistor_119_out), .gate(1'b0));
  Transistor transistor_120 (.in(button_20_out), .out(transistor_119_out), .gate(1'b0));
  Button button_20 (.out(button_20_out));
  Transistor transistor_121 (.in(dipswitch_14_sw1), .out(transistor_121_out), .gate(1'b0));
  Transistor transistor_122 (.in(button_21_out), .out(transistor_121_out), .gate(1'b0));
  Button button_21 (.out(button_21_out));
  Transistor transistor_123 (.in(dipswitch_14_sw8), .out(transistor_90_out), .gate(1'b0));
  Transistor transistor_124 (.in(dipswitch_14_sw8), .out(transistor_101_out), .gate(1'b0));
  Transistor transistor_125 (.in(dipswitch_14_sw8), .out(transistor_91_out), .gate(1'b0));
  Transistor transistor_126 (.in(dipswitch_14_sw8), .out(transistor_93_out), .gate(1'b0));
  Transistor transistor_127 (.in(dipswitch_14_sw8), .out(transistor_104_out), .gate(1'b0));
  Transistor transistor_128 (.in(dipswitch_14_sw8), .out(transistor_106_out), .gate(1'b0));
  Transistor transistor_129 (.in(dipswitch_14_sw8), .out(transistor_107_out), .gate(1'b0));
  Transistor transistor_130 (.in(dipswitch_14_sw8), .out(transistor_110_out), .gate(1'b0));
  Transistor transistor_131 (.in(undriven_38), .out(transistor_131_out), .gate(1'b0));
  Transistor transistor_132 (.in(undriven_39), .out(transistor_132_out), .gate(1'b0));
  Transistor transistor_133 (.in(undriven_40), .out(transistor_133_out), .gate(1'b0));
  Transistor transistor_134 (.in(undriven_41), .out(transistor_134_out), .gate(1'b0));
  Transistor transistor_135 (.in(undriven_42), .out(transistor_135_out), .gate(1'b0));
  Transistor transistor_136 (.in(undriven_43), .out(transistor_136_out), .gate(1'b0));
  Transistor transistor_137 (.in(undriven_44), .out(transistor_137_out), .gate(1'b0));
  Transistor transistor_138 (.in(undriven_45), .out(transistor_138_out), .gate(1'b0));
  DipSwitch dipswitch_14 (.sw1(dipswitch_14_sw1), .sw8(dipswitch_14_sw8));  // open: sw2, sw3, sw4, sw5, sw6, sw7

  // Notes on the sheet:
  //   8 bit Buffer - A
  //   8 bit Buffer - B
  //   S
  //   E
  //   R
  //   S
  //   E
  //   R
  //   Q
  //   Q
  //   A
  //   B7
  //   B
  //   Carry
  //   Carry IN
  //   S
  //   E
  //   R
  //   S
  //   E
  //   R
  //   A
  //   B
  //   Carry IN
  //   Q
  //   B6
  //   Q
  //   S
  //   E
  //   R
  //   S
  //   E
  //   R
  //   A
  //   B
  //   Q
  //   Carry IN
  //   B5
  //   Q
  //   S
  //   E
  //   R
  //   A
  //   S
  //   E
  //   R
  //   B
  //   Carry IN
  //   Q
  //   B4
  //   Q
  //   A
  //   S
  //   E
  //   R
  //   S
  //   B
  //   E
  //   R
  //   Carry IN
  //   Q
  //   Q
  //   B3
  //   A
  //   B
  //   S
  //   E
  //   R
  //   S
  //   E
  //   R
  //   Carry IN
  //   8 bit Binary Counter
  //   A
  //   Q
  //   B2
  //   Q
  //   B
  //   S
  //   Carry IN
  //   E
  //   R
  //   S
  //   E
  //   R
  //   A
  //   Q
  //   B
  //   B1
  //   Q
  //   S
  //   E
  //   R
  //   Carry IN
  //   S
  //   E
  //   R
  //   K
  //   Q
  //   B0
  //   Q
  //   OUTPUT ENABLE
  //   ->
  //   ->
  //   ->
  //   ->
  //   ->
  //   OUTPUT ENABLE
  //   ->
  //   ->
  //   ->
  //   ->
  //   ->
  //   ->
  //   ->
  //   ->
  //   ->
  //   ->
  //   ->
  //   RESET
  //   ENABLE
  //   RESET
  //   ENABLE
  //   ->
  //   ->
  //   ->
  //   ->
  //   ->
  //   ->
  //   ->
  //   ->
  //   ->
  //   A0
  //   A0
  //   A1
  //   A1
  //   A2
  //   A2
  //   A3
  //   A3
  //   Data Bus
  //   A4
  //   A4
  //   A5
  //   A5
  //   A6
  //   A6
  //   A7
  //   A7
  //   A8 (Carry Bit)
  //   A8 (Carry Bit)
  //   A9
  //   A10
  //   A10
  //   A11
  //   A11
  //   A12
  //   A13
  //   A12
  //   A13
  //   A14
  //   A14
  //   A15
  //   A15
  //   A16
  //   A16
  //   ->
  //   ->
  //   ->
  //   ->
  //   ->
  //   ->
  //   ->
  //   ->
  //   ->
  //   ->
  //   ->
  //   ->
  //   ->
  //   ->
  //   ->
  //   ->
  //   ->
  //   ->
  //   ->
  //   ->
  //   ->
  //   ->
  //   ->
  //   ->
  //   ->
  //   ->
  //   ->
  //   ->
  //   ->
  //   ->
  //   ->
  //   ->
  //   ->
  //   ->
  //   ->
  //   ->
  //   ->
  //   ->
  //   ->
  //   ->
  //   ->
  //   ->
  //   ->
  //   ->
  //   ->
  //   ->
  //   ->
  //   ->
  //   ->
  //   ->
  //   ->
  //   ->
  //   ->
  //   ->
  //   ->
  //   ->
  //   ->
  //   ->
  //   ->
  //   ->
  //   ->
  //   ->
  //   ->
  //   ->
  //   A
  //   Sum
  //   B
  //   Carry IN
  //   S
  //   E
  //   R
  //   S
  //   E
  //   R
  //   S
  //   E
  //   R
  //   S
  //   E
  //   R
  //   S
  //   E
  //   R
  //   S
  //   E
  //   R
  //   S
  //   E
  //   R
  //   S
  //   E
  //   R
  //   Carry OUT
  //   Q
  //   Q
  //   Q
  //   Q
  //   Q
  //   Q
  //   Q
  //   Q
  //   A
  //   S
  //   E
  //   R
  //   S
  //   E
  //   R
  //   S
  //   E
  //   R
  //   S
  //   E
  //   R
  //   S
  //   E
  //   R
  //   S
  //   E
  //   R
  //   S
  //   E
  //   R
  //   S
  //   E
  //   R
  //   B
  //   Sum
  //   Carry OUT
  //   Carry IN
  //   Q
  //   Q
  //   Q
  //   Q
  //   Q
  //   Q
  //   Q
  //   Q
  //   A
  //   S
  //   E
  //   R
  //   S
  //   E
  //   R
  //   S
  //   E
  //   R
  //   S
  //   E
  //   R
  //   S
  //   E
  //   R
  //   S
  //   E
  //   R
  //   S
  //   E
  //   R
  //   S
  //   E
  //   R
  //   B
  //   Sum
  //   Carry IN
  //   Carry OUT
  //   Q
  //   Q
  //   Q
  //   Q
  //   Q
  //   Q
  //   Q
  //   Q
  //   A
  //   B
  //   S
  //   E
  //   R
  //   S
  //   E
  //   R
  //   S
  //   E
  //   R
  //   S
  //   E
  //   R
  //   S
  //   E
  //   R
  //   S
  //   E
  //   R
  //   S
  //   E
  //   R
  //   S
  //   E
  //   R
  //   Sum
  //   Carry OUT
  //   Carry IN
  //   A
  //   Q
  //   Q
  //   Q
  //   Q
  //   Q
  //   Q
  //   Q
  //   Q
  //   B
  //   Sum
  //   S
  //   E
  //   R
  //   S
  //   E
  //   R
  //   S
  //   E
  //   R
  //   S
  //   E
  //   R
  //   S
  //   E
  //   R
  //   S
  //   E
  //   R
  //   S
  //   E
  //   R
  //   S
  //   E
  //   R
  //   Carry OUT
  //   Carry IN
  //   A
  //   B
  //   Q
  //   Q
  //   Q
  //   Q
  //   Q
  //   Q
  //   Q
  //   Q
  //   Sum
  //   Carry OUT
  //   Carry IN
  //   S
  //   E
  //   R
  //   S
  //   E
  //   R
  //   S
  //   E
  //   R
  //   S
  //   E
  //   R
  //   S
  //   E
  //   R
  //   S
  //   E
  //   R
  //   S
  //   E
  //   R
  //   S
  //   E
  //   R
  //   A
  //   B
  //   Sum
  //   Carry OUT
  //   Carry IN
  //   Q
  //   Q
  //   Q
  //   Q
  //   Q
  //   Q
  //   Q
  //   Q
  //   S
  //   E
  //   R
  //   S
  //   E
  //   R
  //   S
  //   E
  //   R
  //   S
  //   E
  //   R
  //   S
  //   E
  //   R
  //   S
  //   E
  //   R
  //   S
  //   E
  //   R
  //   S
  //   E
  //   R
  //   A
  //   B
  //   Sum
  //   Carry IN
  //   Q
  //   Q
  //   Q
  //   Q
  //   Q
  //   Q
  //   Q
  //   Q
  //   Carry OUT
  //   S
  //   E
  //   R
  //   S
  //   E
  //   R
  //   S
  //   E
  //   R
  //   S
  //   E
  //   R
  //   S
  //   E
  //   R
  //   S
  //   E
  //   R
  //   S
  //   E
  //   R
  //   S
  //   E
  //   R
  //   Sum
  //   Carry
  //   Q
  //   Q
  //   Q
  //   Q
  //   Q
  //   Q
  //   Q
  //   Q
  //   INPUT ENABLE
  //   OUT Enable
  //   OUT Enable
  //   OUT Enable
  //   INPUT ENABLE
  //   RESET
  //   INPUT ENABLE
  //   OUT Enable
  //   RESET
  //   RESET
  //   OUT Enable
  //   RESET
  //   OUT Enable
  //   OUT Enable
  //   RESET
  //   RESET
  //   OUT Enable
  //   IN Enable
  //   Diode
  //   ->
  //   ->
  //   IN Enable
  //   ->
  //   IN Enable
  //   IN Enable
  //   RESET
  //   Diode
  //   ->
  //   ->
  //   IN Enable
  //   Diode
  //   ->
  //   ->
  //   ->
  //   ->
  //   ->
  //   ->
  //   ->
  //   ->
  //   ->
  //   ->
  //   ->
  //   ->
  //   ->
  //   RESET
  //   Diode
  //   ->
  //   ->
  //   RESET
  //   Diode
  //   ->
  //   ->
  //   ->
  //   Diode
  //   ->
  //   ->
  //   IN Enable
  //   Diode
  //   ->
  //   ->
  //   IN Enable
  //   ->
  //   RESET
  //   Diode
  //   ->
  //   ->
  //   IN Enable
  //   RESET
  //   RESET
  //   ->
  //   RESET
  //   ->
  //   RESET
  //   ->
  //   RESET
  //   ->
  //   Clear All Register
  //   ->
  //   ->
  //   ->
  //   ->
  //   ->
  //   ->
  //   ->
  //   Register A
  //   Register B
  //   Register C
  //   Register D
  //   Register E
  //   Register F
  //   Register G
  //   ->
  //   ->
  //   ->
  //   ->
  //   ->
  //   ->
  //   ->
  //   ->
  //   Register H
  //   RESET
  //   Enable
endmodule
